// Digital circuit pc-and-rom.dig as structural Verilog
module pc_and_rom (
  input  clk,
  input  [7:0] br_to,
  input  br_en,
  output [7:0] word
);

  wire [7:0] add_1_s, multiplexer_1_out, register_1_q;

  Add #(.Bits(8)) add_1 (.a(register_1_q), .b(8'h1), .c_i(1'b0), .s(add_1_s));  // open: c_o
  Multiplexer #(.Bits(8)) multiplexer_1 (.sel(br_en), .in_0(add_1_s), .in_1(br_to), .out(multiplexer_1_out));
  Register #(.Bits(8)) register_1 (.D(multiplexer_1_out), .C(clk), .en(1'b1), .Q(register_1_q));
  ROM #(.AddrBits(8), .Bits(8)) rom_1 (.A(register_1_q), .sel(1'b1), .D(word));

  // Other names for the same wires on the sheet: clock = clk

  // Notes on the sheet:
  //   contents of rom_1 (hex, n*v repeats v):
  //   21,50,3
endmodule
